# Fritzing sketch carousal project (saved by Fritzing 0.9.3b)

parts:
  M1 = Stepper Motor - Bipolar
  A1 = DM860A Stepper Motor Driver
  JACK1 = 2.1mm Barrel Jack with Terminal Block
  JP1 = Header 4 [package=jst-4-pth]

nets:
  N1: M1.A, A1.A+
  N2: M1.C, A1.A-
  N3: M1.B, A1.B+
  N4: M1.D, A1.B-
  N5: A1.VDC, JACK1.POS
  N6: A1.GND, JACK1.NEG
  N7: A1.ENBL-(ENB), A1.DIR-(DIR), A1.PUL-(PUL), JP1.1
  N8: A1.ENBL+(+5V), JP1.2
  N9: A1.DIR+(+5V), JP1.3
  N10: A1.PUL+(+5V), JP1.4

custom parts:
  DM860A Stepper Motor Driver: DM860A is a type of two-phase hybrid stepping motor driver, The drive voltage of which is from 24VDC to 80VDC. It is designed for use with 2-phase hybrid stepper motor of all kinds with 57mm to 110mm outside diameter and less than 8.0A phase current. Mar 2023: Correct pcb layerId as the part won't save correctly in a .fzz file as is.
